# Fritzing sketch educational-robot-explorer (saved by Fritzing 0.9.2b)
breadboards: 1

parts:
  Parte1 = Arduino Uno (Rev3)  # not connected
  Parte3 = Arduino ProtoShield
  J1 = Infrared Proximity Sensor
  M2 = DC Motor
  LED1 = LED - 5mm [color="White (8000K)" package="5 mm [THT]"]
  R1 = Resistor [tolerance=±5% resistance=4.7k package=THT]
  R2 = Photocell (LDR) [package=THT]
  Q2 = PHOTOTRANSISTOR REFLECTIVE OBJECT SENSOR [package=qrb1114-side]
  LED2 = LED - 5mm [color="White (8000K)" package="5 mm [THT]"]
  LED3 = LED - 5mm [color="White (8000K)" package="5 mm [THT]"]
  LED4 = LED - 5mm [color="White (8000K)" package="5 mm [THT]"]
  LED5 = LED - 5mm [color="White (8000K)" package="5 mm [THT]"]
  R3 = Resistor [tolerance=±5% resistance=27 package=THT]
  R4 = Resistor [tolerance=±5% resistance=4.7k package=THT]
  R5 = Resistor [tolerance=±5% resistance=4.7k package=THT]
  R6 = Photocell (LDR) [package=THT]
  Q3 = PHOTOTRANSISTOR REFLECTIVE OBJECT SENSOR [package=qrb1114-side]
  Q1 = NPN-Transistor [package="TO92 [THT]"]
  U1 = L298 [package=multiwatt15_6400bgheatsink]
  M3 = DC Motor

nets:
  N1: Parte3.RES, Parte3.D2, Parte3.5V
  N2: Parte3.LED2, Parte3.D4
  GND: Parte3.GND, J1.GND, Q2.K, R4.Pin_0, R5.Pin_0, Q3.K, Q1.E, U1.GND
  VIN: Parte3.VIN, J1.Vcc, LED1.anode, R2.pin_0, Q2.A, LED2.anode, LED3.anode, LED4.anode, LED5.anode, R6.pin_0, Q3.A, U1.VS, U1.VLS
  N3: Parte3.D3, R1.Pin_0
  N4: Parte3.D5, U1.IN1
  N5: Parte3.D6, U1.IN2
  N6: Parte3.A4, Q3.C
  N7: Parte3.A3, Q2.C
  N8: Parte3.A2, R4.Pin_1, R6.pin_1
  N9: Parte3.A1, R2.pin_1, R5.Pin_1
  N10: Parte3.A0, J1.Vout
  N11: Parte3.D9, U1.IN3
  N12: Parte3.D10, U1.IN4
  N13: M2.pin_1, U1.OUT3
  N14: M2.pin_2, U1.OUT4
  N15: LED1.cathode, LED2.cathode, LED3.cathode, LED4.cathode, LED5.cathode, R3.Pin_0
  N16: R1.Pin_1, Q1.B
  N17: R3.Pin_1, Q1.C
  N18: U1.OUT1, M3.pin_1
  N19: U1.OUT2, M3.pin_2

notes:
  Modulos TCRT5000 con salida digital mediante comparador.
  VCC - rojo
  GND - negro
  D0 - verde
  A0 - N/C
  Modulo L298N
  ENA - jumper (motor1)
  IN1 - marron (motor1)
  IN2 - marron (motor1)
  IN3 - morado (motor2)
  IN4 - morado (motor2)
  ENB - jumper (motor2)
  +12V - rojo
  GND - negro
  +5V - rojo (jumper int. deshab.)
  OUT1 - naranja +(motor1)
  OUT2 - azul - (motor1)
  OUT3 - naranja +(motor2)
  OUT4 - azul - (motor2)
  servomotores de rotacion continua
